# Fritzing sketch emonMeter (saved by Fritzing 0.9.3b)
perfboards: 1

parts:
  R1 = Resistor [tolerance=±5% resistance=10k package=THT]
  R2 = Resistor [tolerance=±5% resistance=10k package=THT]
  R3 = Resistor [tolerance=±5% resistance=10k package=THT]
  R4 = Resistor [tolerance=±5% resistance=10k package=THT]
  part = Resistor [tolerance=±5% resistance=10k package=THT]
  R5 = Resistor [tolerance=±5% resistance=10k package=THT]
  J2 = female pin header, 2 pins [form="♀ (female)"]
  J1 = female pin header, 2 pins [form="♀ (female)"]
  J4 = female pin header, 2 pins [form="♀ (female)"]
  J3 = female pin header, 2 pins [form="♀ (female)"]
  J6 = female pin header, 2 pins [form="♀ (female)"]
  J5 = female pin header, 2 pins [form="♀ (female)"]
  Part1 = Arduino Pro Mini v13
  RFM69_W/CW = RFM69HCW ISM Transciever

nets:
  N1: R1.Pin_0, J1.pin2, Part1.D4
  GND: R1.Pin_1, R2.Pin_1, R3.Pin_1, R4.Pin_1, part.Pin_1, R5.Pin_1, Part1.GND, RFM69_W/CW.1_GND
  N2: R2.Pin_0, J2.pin2, Part1.D5_PWM
  N3: R3.Pin_0, J3.pin2, Part1.D6_PWM
  N4: R4.Pin_0, J4.pin2, Part1.D7
  N5: part.Pin_0, J6.pin2, Part1.D9_PWM
  N6: R5.Pin_0, J5.pin2, Part1.D8
  N7: J2.pin1, J1.pin1, J4.pin1, J3.pin1, J6.pin1, J5.pin1, Part1.VCC, RFM69_W/CW.13_3.3V
  N8: Part1.D13/SCK, RFM69_W/CW.4_SCK
  N9: Part1.D12/MISO, RFM69_W/CW.2_MISO
  N10: Part1.D11_PWM/MOSI, RFM69_W/CW.3_MOSI
  N11: Part1.D10_PWM/SS, RFM69_W/CW.5_NSS_(CS)
  N12: Part1.D2, RFM69_W/CW.14_DIO0

notes:
  RFM69

custom parts:
  RFM69HCW ISM Transciever: RF Transceiver by Hope RF. Well supported Arduino libraries are available. This ISM band transceiver is available in several frequencies e.g. 433MHz and 915MHz and it is also available in various feature versions.
